# Fritzing sketch ShemaElectrique (saved by Fritzing 0.9.2b)
breadboards: 1

parts:
  Part2 = Arduino Mega 2560 (Rev3)
  Force_Sensitive_Resitor_1 = Basic Force Sensing Resistor (FSR) [package=THT]
  R1 = Resistor [tolerance=±5% resistance=1k package="2512 [SMD]"]
  Force_Sensitive_Resitor_2 = Basic Force Sensing Resistor (FSR) [package=THT]
  R2 = Resistor [tolerance=±5% resistance=1k package="2512 [SMD]"]
  Force_Sensitive_Resitor_3 = Basic Force Sensing Resistor (FSR) [package=THT]
  R3 = Resistor [tolerance=±5% resistance=1k package="2512 [SMD]"]
  Force_Sensitive_Resitor_4 = Basic Force Sensing Resistor (FSR) [package=THT]
  R4 = Resistor [tolerance=±5% resistance=1k package="2512 [SMD]"]
  Force_Sensitive_Resitor_5 = Basic Force Sensing Resistor (FSR) [package=THT]
  R5 = Resistor [tolerance=±5% resistance=1k package="2512 [SMD]"]
  Force_Sensitive_Resitor_6 = Basic Force Sensing Resistor (FSR) [package=THT]
  R6 = Resistor [tolerance=±5% resistance=1k package="2512 [SMD]"]
  Force_Sensitive_Resitor_7 = Basic Force Sensing Resistor (FSR) [package=THT]
  R7 = Resistor [tolerance=±5% resistance=1k package="2512 [SMD]"]
  Force_Sensitive_Resitor_8 = Basic Force Sensing Resistor (FSR) [package=THT]
  R8 = Resistor [tolerance=±5% resistance=1k package="2512 [SMD]"]
  Force_Sensitive_Resitor_9 = Basic Force Sensing Resistor (FSR) [package=THT]
  R9 = Resistor [tolerance=±5% resistance=1k package="2512 [SMD]"]
  Force_Sensitive_Resitor_10 = Basic Force Sensing Resistor (FSR) [package=THT]
  R10 = Resistor [tolerance=±5% resistance=1k package="2512 [SMD]"]
  Force_Sensitive_Resitor_11 = Basic Force Sensing Resistor (FSR) [package=THT]
  R11 = Resistor [tolerance=±5% resistance=1k package="2512 [SMD]"]
  Force_Sensitive_Resitor_12 = Basic Force Sensing Resistor (FSR) [package=THT]
  R12 = Resistor [tolerance=±5% resistance=1k package="2512 [SMD]"]
  Force_Sensitive_Resitor_13 = Basic Force Sensing Resistor (FSR) [package=THT]
  R13 = Resistor [tolerance=±5% resistance=1k package="2512 [SMD]"]
  Force_Sensitive_Resitor_14 = Basic Force Sensing Resistor (FSR) [package=THT]
  R14 = Resistor [tolerance=±5% resistance=1k package="2512 [SMD]"]
  Force_Sensitive_Resitor_15 = Basic Force Sensing Resistor (FSR) [package=THT]
  R15 = Resistor [tolerance=±5% resistance=1k package="2512 [SMD]"]
  Force_Sensitive_Resitor_16 = Basic Force Sensing Resistor (FSR) [package=THT]
  R16 = Resistor [tolerance=±5% resistance=1k package="2512 [SMD]"]
  U1 = SPM0204UD5 [package=spm0204ud5]
  U2 = SPM0204UD5 [package=spm0204ud5]
  U3 = SPM0204UD5 [package=spm0204ud5]
  U4 = SPM0204UD5 [package=spm0204ud5]
  U5 = SPM0204UD5 [package=spm0204ud5]
  Part3 = Arduino Uno (Rev3)
  NEOPIXEL1 = Neopixel Strip -- White (60/m)
  NEOPIXEL2 = Neopixel Strip -- White (60/m)
  NEOPIXEL3 = Neopixel Strip -- White (60/m)
  Power_plug1 = Power plug

nets:
  N1: Part2.A8, Force_Sensitive_Resitor_9.pin_1, R9.Pin_1
  N2: Part2.A9, Force_Sensitive_Resitor_10.pin_1, R10.Pin_1
  N3: Part2.A10, Force_Sensitive_Resitor_11.pin_1, R11.Pin_1
  N4: Part2.A11, Force_Sensitive_Resitor_12.pin_1, R12.Pin_1
  N5: Part2.A12, Force_Sensitive_Resitor_13.pin_1, R13.Pin_1
  N6: Part2.A13, R14.Pin_1
  N7: Part2.A14, Force_Sensitive_Resitor_15.pin_1, R15.Pin_1
  N8: Part2.A15, Force_Sensitive_Resitor_16.pin_1, R16.Pin_1
  N9: Part2.A0, Force_Sensitive_Resitor_1.pin_1, R1.Pin_1
  N10: Part2.A1, Force_Sensitive_Resitor_2.pin_1, R2.Pin_1
  N11: Part2.A2, Force_Sensitive_Resitor_3.pin_1, R3.Pin_1
  N12: Part2.A3, Force_Sensitive_Resitor_4.pin_1, R4.Pin_1
  N13: Part2.A4, Force_Sensitive_Resitor_5.pin_1, R5.Pin_1
  N14: Part2.A5, Force_Sensitive_Resitor_6.pin_1, R6.Pin_1
  N15: Part2.A6, Force_Sensitive_Resitor_7.pin_1, R7.Pin_1
  N16: Part2.A7, Force_Sensitive_Resitor_8.pin_1, R8.Pin_1
  GND: Part2.GND, R1.Pin_0, R2.Pin_0, R3.Pin_0, R4.Pin_0, R5.Pin_0, R6.Pin_0, R7.Pin_0, R8.Pin_0, R9.Pin_0, R10.Pin_0, R11.Pin_0, R12.Pin_0, R13.Pin_0, R14.Pin_0, R15.Pin_0, R16.Pin_0, U1.GND, U2.GND, U3.GND, U4.GND, U5.GND, Part3.GND, NEOPIXEL1.GND, NEOPIXEL2.GND, NEOPIXEL3.GND, Power_plug1.GND
  N17: Part2.D11_PWM, U5.GND#
  N18: Part2.D10_PWM, U5.OUT
  N19: Part2.D9_PWM, U4.GND#
  N20: Part2.D8_PWM, U4.OUT
  5V: Part2.5V, Force_Sensitive_Resitor_1.pin_0, Force_Sensitive_Resitor_2.pin_0, Force_Sensitive_Resitor_3.pin_0, Force_Sensitive_Resitor_4.pin_0, Force_Sensitive_Resitor_5.pin_0, Force_Sensitive_Resitor_6.pin_0, Force_Sensitive_Resitor_7.pin_0, Force_Sensitive_Resitor_8.pin_0, Force_Sensitive_Resitor_9.pin_0, Force_Sensitive_Resitor_10.pin_0, Force_Sensitive_Resitor_11.pin_0, Force_Sensitive_Resitor_12.pin_0, Force_Sensitive_Resitor_13.pin_0, Force_Sensitive_Resitor_14.pin_0, Force_Sensitive_Resitor_15.pin_0, Force_Sensitive_Resitor_16.pin_0, U1.VS, U2.VS, U3.VS, U4.VS, U5.VS, NEOPIXEL1.+5V, NEOPIXEL2.+5V, NEOPIXEL3.+5V, Power_plug1.VCC
  N21: Part2.D2_PWM, U1.OUT
  N22: Part2.D3_PWM, U1.GND#
  N23: Part2.D4_PWM, U2.OUT
  N24: Part2.D5_PWM, U2.GND#
  N25: Part2.D6_PWM, U3.OUT
  N26: Part2.D7_PWM, U3.GND#
  N27: Part3.D8, NEOPIXEL3.DI
  N28: Part3.D4, NEOPIXEL1.DI
  N29: Part3.D6_PWM, NEOPIXEL2.DI

notes:
  Jeremy Ferland
  Charles-Olivier Belanger

custom parts:
  Neopixel Strip -- White (60/m): Neopixel Strip, White, 60 pixels per meter.
